# Fritzing sketch Untitled Sketch 2 (saved by Fritzing 0.8.7b)

parts:
  Composant2 = Arduino Mega 2560 (Rev3)
  U1 = ESP8266 WiFi Module [part_number=ESP8266]

nets:
  N1: Composant2.D15/RX3, U1.TXD
  N2: Composant2.D14/TX3, U1.RXD
  GND: Composant2.GND, U1.GND
  3V3: Composant2.3V3, U1.VCC

custom parts:
  ESP8266 WiFi Module: Generic WiFi Module based on the ESP8266 with onboard PCB antenna and UART communications
